# Fritzing sketch IR (saved by Fritzing 0.8.3b)
breadboards: 1

parts:
  Part1 = Arduino Uno (Rev3)
  IR1 = TSOP312.., 314.. [package=THT]
  LED1 = LED - 5mm [color="Red (633nm)" package="5 mm [THT]"]
  R1 = Resistor [tolerance=±5% resistance=220 package=THT]

nets:
  N1: Part1.GND, IR1.Vs, LED1.cathode
  N2: Part1.D11_PWM/MOSI, IR1.GND
  N3: Part1.D13/SCK, R1.Pin_0
  N4: Part1.5V, IR1.Data
  N5: LED1.anode, R1.Pin_1

notes:
  SFH 5110
