# Fritzing sketch atmega328_usb_bluetooth_rgb_led (saved by Fritzing 0.8.3b)
breadboards: 1

parts:
  IC1 = MICROCONTROLLER [package=dil28-3]
  R1 = Resistor [tolerance=±5% resistance=10k package=THT]
  S1 = Pushbutton [package="[THT]"]
  R4 = Resistor [tolerance=±5% resistance=1k package=THT]
  R5 = Resistor [tolerance=±5% resistance=1k package=THT]
  R6 = Resistor [tolerance=±5% resistance=1k package=THT]
  LED1 = RGB LED (com. anode, rbg) [package="5 mm [THT]"]
  R7 = Resistor [tolerance=±5% resistance=220 package=THT]
  R8 = Resistor [tolerance=±5% resistance=220 package=THT]
  R9 = Resistor [tolerance=±5% resistance=220 package=THT]
  T1 = LM35 Temperature Sensor [package="TO92 [THT]"]
  R10 = Resistor [tolerance=±5% resistance=10k package=THT]
  R11 = Resistor [tolerance=±5% resistance=10k package=THT]

nets:
  N1: IC1.PC6(_RESET), R1.Pin_0, S1.Pin_1, S1.Pin_2
  N2: IC1.PD2(INT0), R4.Pin_1, R5.Pin_0
  N3: IC1.VCC, IC1.AVCC, R1.Pin_1, LED1.common_anode, T1.+Vs, R10.Pin_0, R11.Pin_0
  GND: IC1.GND, IC1.AGND, S1.Pin_3, S1.Pin_4, R6.Pin_1, T1.GND
  N4: IC1.PD6(AIN0), R9.Pin_0
  N5: IC1.PD7(AIN1), T1.Vout, R10.Pin_1, R11.Pin_1
  N6: IC1.PB1(OC1A), R8.Pin_0
  N7: IC1.PB2(SS_OC1B), R7.Pin_0
  N8: R5.Pin_1, R6.Pin_0
  N9: LED1.red_cathode, R9.Pin_1
  N10: LED1.blue_cathode, R7.Pin_1
  N11: LED1.green_cathode, R8.Pin_1

notes:
  3.3V 5V TX RX GND
  Prolific PL2303
  BT HC-06 Module
  KEY-
  RXD-
  TXD-
  5V-
  3.3V-
  GND-
