# Fritzing sketch bt (saved by Fritzing 0.8.3b)
breadboards: 1

parts:
  Part1 = Arduino Uno (Rev3)
  R1 = Resistor [tolerance=±5% resistance=1k package=THT]
  R2 = Resistor [tolerance=±5% resistance=1k package=THT]
  R3 = Resistor [tolerance=±5% resistance=1k package=THT]
  LED1 = LED - 5mm [color="Green (555nm)" package="5 mm [THT]"]
  R4 = Resistor [tolerance=±5% resistance=100 package=THT]

nets:
  N1: Part1.ICSP_SCK, Part1.D13/SCK, R4.Pin_0
  N2: Part1.GND, R1.Pin_1, LED1.cathode
  N3: Part1.D2, R2.Pin_0, R3.Pin_1
  N4: R1.Pin_0, R2.Pin_1
  N5: LED1.anode, R4.Pin_1

notes:
  BT HC-06 Module
  KEY-
  RXD-
  TXD-
  5V-
  3.3V-
  GND-
