# Fritzing sketch ready to write sketch plus diode (saved by Fritzing 0.8.3b)
breadboards: 1

parts:
  IC1 = MICROCONTROLLER [package=dil28-3]
  R1 = Resistor [tolerance=±5% resistance=10k package=THT]
  R2 = Resistor [tolerance=±5% resistance=220 package=THT]
  S1 = Pushbutton [package="[THT]"]
  LED1 = LED - 5mm [color="Red (633nm)" package="5 mm [THT]"]

nets:
  N1: IC1.PC6(_RESET), R1.Pin_0, S1.Pin_1, S1.Pin_2
  N2: IC1.VCC, IC1.AVCC, R1.Pin_1
  N3: IC1.GND, IC1.AGND, S1.Pin_3, S1.Pin_4, LED1.cathode
  N4: IC1.PB3(MOSI_OC2), R2.Pin_0
  N5: R2.Pin_1, LED1.anode

notes:
  3.3V 5V TX RX GND
  Prolific PL2303
