# Fritzing sketch Ethernet (saved by Fritzing 0.8.4b)
breadboards: 2

parts:
  Part1 = Arduino Leonardo (Rev3b)
  U1 = WIZ811MJ [part_number=ENC28J60 package=wiz811mj]  # not connected
  J1 = shrouded pin header, 10 pins [form="♂ (shrouded male)"]

nets:
  N1: Part1.3V3, J1.pin10
  N2: Part1.D8/A8, J1.pin9

notes:
  ENC28J60
