# Fritzing sketch lampka_230V (saved by Fritzing 0.8.3b)
breadboards: 1

parts:
  R1 = Resistor [tolerance=±5% resistance=220 package=THT]
  R2 = Resistor [tolerance=±5% resistance=220 package=THT]
  R3 = Resistor [tolerance=±5% resistance=330 package=THT]
  R4 = Resistor [tolerance=±5% resistance=330 package=THT]
  Part1 = Arduino Uno (Rev3)
  LED1 = LED - 5mm [color="Red (633nm)" package="5 mm [THT]"]
  U1 = MOC3031-M [package=dil06]
  U2 = TRIAC [package=to-92]
  IR2 = TSOP312.., 314.. [package=THT]

nets:
  N1: R1.Pin_0, R2.Pin_0, Part1.D9_PWM
  N2: R1.Pin_1, LED1.anode
  N3: R2.Pin_1, U1.1
  N4: R3.Pin_0, U1.6
  N5: R3.Pin_1, U2.G
  N6: R4.Pin_0, U1.4
  N7: R4.Pin_1, U2.M2
  N8: Part1.ICSP_SCK, Part1.D13/SCK, IR2.GND
  N9: Part1.GND, LED1.cathode, U1.2, IR2.Vs
  N10: Part1.5V, IR2.Data

notes:
  SFH 5110
  lampka nocna
  230 V
