# Fritzing sketch RFID (saved by Fritzing 0.8.4b)
breadboards: 1

parts:
  Part1 = Arduino Leonardo (Rev3b)
  J1 = Piezo Speaker
  J2 = Basic Servo
  Part2 = RFID USB Reader
  XTAL1 = Crystal [frequency="16 Mhz" package=THT]  # not connected
  MIRF1 = MIRF [package=mirf]

nets:
  N1: Part1.D3_PWM/SCL, MIRF1.7, MIRF1.6, MIRF1.5, MIRF1.4, MIRF1.3, MIRF1.1
  3V3: Part1.3V3, Part2.VCC
  5V: Part1.5V, J2.vcc
  GND: Part1.GND, J1.pin1, J2.gnd
  N2: Part1.D8/A8, J2.pulse
  N3: Part1.D9_PWM/A9, Part2.GND
  N4: Part1.D10_PWM/A10, Part2.GNDT

notes:
  RFID-RC522
