# Fritzing sketch strobo (saved by Fritzing 0.8.3b)
circuit board: 16.9333cm x 5.64444cm
breadboards: 1

parts:
  Part1 = Arduino Uno (Rev3)
  LED1 = LED - 5mm [color="Red (633nm)" package="5 mm [THT]"]
  R1 = Resistor [tolerance=±5% resistance=150 package=THT]
  LED2 = LED - 5mm [color="Red (633nm)" package="5 mm [THT]"]
  LED3 = LED - 5mm [color="Red (633nm)" package="5 mm [THT]"]
  LED4 = LED - 5mm [color="Red (633nm)" package="5 mm [THT]"]
  R2 = Resistor [tolerance=±5% resistance=150 package=THT]
  R3 = Resistor [tolerance=±5% resistance=150 package=THT]
  R4 = Resistor [tolerance=±5% resistance=150 package=THT]
  R5 = Rotary Potentiometer (Small)
  R6 = Resistor [tolerance=±5% resistance=10k package=THT]
  R7 = Resistor [tolerance=±5% resistance=10k package=THT]
  Q1 = npn-Powertransistor [package="TO220 [THT]"]

nets:
  N1: Part1.A0, R6.Pin_0
  N2: Part1.GND, R5.leg2, Q1.emitter
  N3: Part1.D3_PWM, R7.Pin_0
  N4: Part1.5V, R1.Pin_1, R2.Pin_1, R3.Pin_1, R4.Pin_1, R5.leg1
  N5: LED1.anode, R1.Pin_0
  N6: LED2.cathode, LED3.cathode, LED4.cathode, Q1.collector
  N7: LED2.anode, R2.Pin_0
  N8: LED3.anode, R3.Pin_0
  N9: LED4.anode, R4.Pin_0
  N10: R5.wiper, R6.Pin_1
  N11: R7.Pin_1, Q1.base
