# Fritzing sketch styki (saved by Fritzing 0.9.1b)
breadboards: 1

parts:
  R1 = Resistor [tolerance=±5% resistance=150 package=THT]
  R2 = Resistor [tolerance=±5% resistance=150 package=THT]
  R3 = Resistor [tolerance=±5% resistance=150 package=THT]
  S1 = Pushbutton [package="[THT]"]
  S2 = Pushbutton [package="[THT]"]
  LED1 = LED - 5mm [color="Green (555nm)" package="5 mm [THT]"]
  LED2 = LED - 5mm [color="Yellow (585nm)" package="5 mm [THT]"]
  LED3 = LED - 5mm [color="Green (555nm)" package="5 mm [THT]"]
  R4 = Resistor [tolerance=±5% resistance=10k package=THT]
  R5 = Resistor [tolerance=±5% resistance=10k package=THT]
  Part1 = Arduino Uno (Rev3)

nets:
  N1: R1.Pin_0, Part1.D9_PWM
  N2: R1.Pin_1, LED1.anode
  N3: R2.Pin_0, Part1.D10_PWM/SS
  N4: R2.Pin_1, LED2.anode
  N5: R3.Pin_0, Part1.D11_PWM/MOSI
  N6: R3.Pin_1, LED3.anode
  N7: S1.Pin_1, S1.Pin_2, R5.Pin_1, Part1.D2
  N8: S1.Pin_3, S1.Pin_4, S2.Pin_3, S2.Pin_4, Part1.5V
  N9: S2.Pin_1, S2.Pin_2, R4.Pin_0, Part1.D3_PWM
  N10: LED1.cathode, LED2.cathode, LED3.cathode, R4.Pin_1, R5.Pin_0, Part1.GND
